# Fritzing sketch raspberry schematic (saved by Fritzing 0.8.7b)
stripboards: 1

parts:
  Part1 = Adafruit VL6180X Time of Flight Distance Sensor [part_number="Adafruit #3316"]
  Raspberry_Pi_B_rev1 = Raspberry Pi B rev2
  Part4 = NeoPixel Stick [part_number=1426]
  Part5 = NeoPixel Stick [part_number=1426]
  Part6 = NeoPixel Stick [part_number=1426]
  Q1 = Basic FET N-Channel [package="TO220 [THT]"]
  Q2 = Basic FET N-Channel [package="TO220 [THT]"]
  Q3 = Basic FET N-Channel [package="TO220 [THT]"]
  VCC1 = Battery
  R1 = Resistor [package="2010 [SMD]"]
  R3 = Resistor [package="2010 [SMD]"]
  R4 = Resistor [package="2010 [SMD]"]

nets:
  VIN: Part1.VIN, Raspberry_Pi_B_rev1.3V3
  GND: Part1.GND, Raspberry_Pi_B_rev1.GND, Raspberry_Pi_B_rev1.GPIO_17, Raspberry_Pi_B_rev1.GPIO_18, Raspberry_Pi_B_rev1.GPIO_27, Part5.DATAOUT, Part6.DATAOUT, Q1.gate, Q1.source, Q2.gate, Q2.source, Q3.gate, Q3.source, VCC1.-, VCC1.+, R1.Pin_0, R1.Pin_1, R3.Pin_0, R3.Pin_1, R4.Pin_0, R4.Pin_1
  N1: Part1.SCL, Raspberry_Pi_B_rev1.GPIO_3
  N2: Part1.SDA, Raspberry_Pi_B_rev1.GPIO_2
  N3: Part4.+5V, Q2.drain
  N4: Part5.+5V, Q1.drain
  N5: Part6.+5V, Q3.drain

notes:
  Usepins: 4x mosfet pwm --> (GPIO12 GPIO13 GPIO18 & GPIO19)
  Required: SCL, SCA, 5V/3.3V, Ground
  [mosfet voor halogeen + RC circuit]

custom parts:
  Adafruit VL6180X Time of Flight Distance Sensor: The VL6180X is a Time of Flight distance sensor like no other you've used! The sensor contains a very tiny invisible laser source, and a matching sensor. The VL6180X can detect the "time of flight", or how long the light has taken to bounce back to the sensor. Since it uses a very narrow light source, it is good for determining distance of only the surface directly in front of it. Unlike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
  NeoPixel Stick: Make your own little LED strip arrangement with this stick of NeoPixel LEDs. We crammed 8 of the tiny 5050 (5mm x 5mm) smart RGB LEDs onto a PCB with mounting holes and a chainable design. Use only one microcontroller pin to control as many as you can chain together! Each LED is addressable as the driver chip is inside the LED. Each one has ~18mA constant current drive so the color will be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
